# Fritzing sketch schema (saved by Fritzing 0.9.9b)
breadboards: 2

parts:
  J1 = STM32 Nucleo boards
  LED1 = smd LED [color="Red (633nm)" package="0805 [SMD]"]
  R1 = Resistor [tolerance=±5% resistance=220 package="0603 [SMD]"]
  R2 = Resistor [tolerance=±5% resistance=220 package="0603 [SMD]"]
  LED2 = smd LED [color="Blue (470nm)" package="0603 [SMD]"]

nets:
  N1: J1.A1, R2.Pin_1
  N2: J1.D11_PWM/MOSI, R1.Pin_1
  N3: J1.GND, LED1.cathode, LED2.cathode
  N4: LED1.anode, R1.Pin_0
  N5: R2.Pin_0, LED2.anode

notes:
  pulse oxi
  RTC
  OLED
  temp
